# Fritzing sketch tamagotchi_wiring_diagram (saved by Fritzing 0.9.5d)
breadboards: 1

parts:
  Part1 = Arduino Uno (Rev3) - ICSP
  OLED1 = SSD1306 0.96in 128x64 I2C Monochrome OLED Display
  S1 = Momentary Switch [package=ksa_sealed_tac_switch]
  S2 = Momentary Switch [package=ksa_sealed_tac_switch]

nets:
  N1: Part1.A4/SDA, OLED1.SDA
  N2: Part1.A5/SCL, OLED1.SCL
  N3: Part1.D2, S2.4
  GND: Part1.GND, OLED1.GND, S1.1, S2.1
  VIN: Part1.VIN, OLED1.VCC

notes:
  Vcc->Vin
  scl->A5
  SDA ->A4
  Ground both buttons
